# Fritzing sketch remote-estop (saved by Fritzing 0.9.3b)

parts:
  WeMos_D1_Mini_Battery_Shield1 = WeMos D1 Mini Battery Shield
  S1 = Round Pushbutton
  WeMos_D1_Mini1 = WeMos D1 Mini
  R1 = Resistor [tolerance=±5% resistance=220 package=THT]

nets:
  5V: WeMos_D1_Mini_Battery_Shield1.5V, WeMos_D1_Mini1.5V
  N1: WeMos_D1_Mini_Battery_Shield1.G, WeMos_D1_Mini1.G, R1.Pin_0
  N2: S1.leg0, WeMos_D1_Mini1.3V3
  N3: S1.leg1, WeMos_D1_Mini1.D2, R1.Pin_1
